# Fritzing sketch branchement (saved by Fritzing 0.9.2b)

parts:
  Part1 = Iteaduino UNO
  J1 = Basic Servo
  J2 = Basic Servo  # not connected
  Part2 = Bluetooth HC-05 Macho

nets:
  N1: Part1.D0, Part2.RXD
  N2: Part1.RX, Part2.TXD
  VCC: Part1.VCC, Part2.VCC
  N3: Part1.GND#174, J1.gnd
  N4: Part1.GND#183, Part2.GND

custom parts:
  Iteaduino UNO: Breakout board Platform Based On Arduino by Iteadstudio Principal features : Electronic Brick Ports 3.3V or 5V power supply The official support forum: support@iteadstudio.com
